// Logisim project CORDIC.circ as structural Verilog: 10 circuits, main circuit main
module main (
  input  [7:0] data,
  input  data_av,
  input  start,
  output done,
  output [31:0] sen,
  output [31:0] cos
);

  wire clk, cordic_1_mem, reset;
  wire [4:0] cordic_1_i;
  wire [31:0] reg_mem_q, rom_1_data;

  Clock u_clk (.out(clk));
  Button u_reset (.out(reset));
  CORDIC cordic_1 (
    .in_5(clk), .in_6(reset), .data(data), .reg_mem(reg_mem_q), .i(cordic_1_i), .data_av(data_av),
    .start(start), .mem(cordic_1_mem), .done(done), .sen(sen), .cos(cos));  // open: Current_State
  ROM #(.addrWidth(5), .dataWidth(32)) rom_1 (.addr(cordic_1_i), .data(rom_1_data), .sel(cordic_1_mem));
  Register #(.width(32)) reg_mem (.D(rom_1_data), .en(cordic_1_mem), .Q(reg_mem_q), .clk(clk), .clr(reset));

  // Notes on the sheet:
  //   contents of rom_1 (hex, n*v repeats v):
  //   2d000000 1a90a731 e094740 7200112 3938aa6 1ca3794 e52a1a 7296d7 394ba5 1ca5d9 e52ed 72976 394bb
  //   1ca5d e52e 7297 394b 1ca5 e52 729 394 1ca e5 72 39 1c e 7 3 1
endmodule

module CORDIC (
  input  [7:0] data,
  input  data_av,
  input  [31:0] reg_mem,
  input  start,
  input  in_5,
  input  in_6,
  output [3:0] Current_State,
  output [4:0] i,
  output [31:0] cos,
  output [31:0] sen,
  output mem,
  output done
);

  wire control_path_1_wr_ang_rs_xysa, control_path_1_wr_i, control_path_1_wr_it_rs_i, control_path_1_wr_sa,
       control_path_1_wr_xnew_rs_shifr, control_path_1_wr_xy, control_path_1_wr_ynew, data_path_1_neg,
       data_path_1_zero, Sincronizador_bt_out;
  wire [2:0] control_path_1_rs_m1, control_path_1_rs_m2;
  wire [31:0] data_path_1_i;

  BitSelector #(.width(32), .group(5)) bitselector_1 (.in(data_path_1_i), .out(i), .sel(3'b000));
  Data_Path data_path_1 (
    .reg_mem(reg_mem), .zero(data_path_1_zero), .neg(data_path_1_neg), .rs_m1(control_path_1_rs_m1),
    .rs_m2(control_path_1_rs_m2), .clk(in_5), .reset(in_6), .wr_i(control_path_1_wr_i), .i(data_path_1_i),
    .wr_xNew_rs_shifr(control_path_1_wr_xnew_rs_shifr), .wr_sA(control_path_1_wr_sa),
    .wr_xy(control_path_1_wr_xy), .wr_it_rs_i(control_path_1_wr_it_rs_i), .wr_yNew(control_path_1_wr_ynew),
    .data(data), .wr_ang_rs_xySa(control_path_1_wr_ang_rs_xysa), .sen(sen), .cos(cos), .done(done));
  Control_Path control_path_1 (
    .zero(data_path_1_zero), .neg(data_path_1_neg), .rs_m1(control_path_1_rs_m1),
    .rs_m2(control_path_1_rs_m2), .data_av(Sincronizador_bt_out), .start(start), .in_5(in_5), .in_6(in_6),
    .Current_State(Current_State), .wr_yNew(control_path_1_wr_ynew), .wr_xy(control_path_1_wr_xy),
    .wr_i(control_path_1_wr_i), .wr_sA(control_path_1_wr_sa),
    .wr_xNew_rs_shifr(control_path_1_wr_xnew_rs_shifr), .wr_ang_rs_xySa(control_path_1_wr_ang_rs_xysa),
    .wr_it_rs_i(control_path_1_wr_it_rs_i), .done(done), .MEM(mem));
  synch Sincronizador (.bt_out(Sincronizador_bt_out), .bt_in(data_av), .clk(in_5), .reset(in_6));

  // Other names for the same wires on the sheet: clk = in_5; reset = in_6
endmodule

module synch (
  input  bt_in,
  input  clk,
  input  reset,
  output bt_out
);

  wire and_1_out, and_2_out, FF0_q, FF1_q, not_1_out, not_2_out, not_3_out, or_1_out;

  not not_1 (not_1_out, FF1_q);
  not not_2 (not_2_out, FF0_q);
  or or_1 (or_1_out, FF1_q, FF0_q);
  and and_1 (and_1_out, or_1_out, bt_in);
  and and_2 (and_2_out, not_1_out, not_2_out, bt_in);
  D_Flip_Flop FF1 (.clk(clk), .D(and_1_out), .Q(FF1_q), .reset(reset));  // open: Qn, preset, en
  D_Flip_Flop FF0 (.clk(clk), .D(and_2_out), .Q(FF0_q), .reset(reset));  // open: Qn, preset, en
  not not_3 (not_3_out, FF1_q);
  and and_3 (bt_out, not_3_out, FF0_q);
endmodule

// SOMADOR
module Somador (
  input  [31:0] x,
  input  [31:0] y,
  input  [31:0] reg_it,
  input  [31:0] sumAngle,
  input  [31:0] reg_mem,
  input  [31:0] reg_i,
  input  [31:0] angle,
  input  rs_shiftr,
  input  [2:0] rs_m1,
  input  [2:0] rs_m2,
  output [31:0] soma_out,
  output neg,
  output zero
);

  wire bitselector_1_out;
  wire [31:0] multiplexer_1_out, multiplexer_2_out, not_1_out, not_2_out, not_3_out,
       shift_right_i_1_nshiftr_out, shift_right_i_1_shiftr_out;

  Multiplexer #(.select(3), .width(32), .enable("false")) multiplexer_1 (
    .in0(32'h1), .in1(x), .in2(y), .in3(reg_it), .in4(sumAngle), .out(multiplexer_1_out), .sel(rs_m1));  // open: in5, in6, in7
  nor nor_1 (zero, soma_out[16], neg, soma_out[30], soma_out[29], soma_out[28], soma_out[27], soma_out[26], soma_out[25], soma_out[24], soma_out[23], soma_out[22], soma_out[21], soma_out[20], soma_out[19], soma_out[18], soma_out[17], soma_out[15], soma_out[14], soma_out[13], soma_out[12], soma_out[11], soma_out[10], soma_out[9], soma_out[8], soma_out[7], soma_out[6], soma_out[5], soma_out[4], soma_out[3], soma_out[2], soma_out[1], soma_out[0]);
  Shift_Right_i shift_right_i_1 (
    .x(x), .y(y), .reg_i(reg_i), .shiftr_out(shift_right_i_1_shiftr_out), .rs_shiftr(rs_shiftr),
    .nshiftr_out(shift_right_i_1_nshiftr_out));
  assign not_1_out = ~reg_i;  // NOT_Gate not_1, 32 bits wide
  assign not_2_out = ~reg_mem;  // NOT_Gate not_2, 32 bits wide
  Multiplexer #(.select(3), .width(32), .enable("false")) multiplexer_2 (
    .in0(reg_mem), .in1(shift_right_i_1_shiftr_out), .in2(reg_i), .in4(not_2_out),
    .in5(shift_right_i_1_nshiftr_out), .in6(not_1_out), .in7(not_3_out), .out(multiplexer_2_out), .sel(rs_m2));  // open: in3
  BitSelector #(.width(3)) bitselector_1 (.in(rs_m2), .out(bitselector_1_out), .sel(2'b10));
  assign not_3_out = ~angle;  // NOT_Gate not_3, 32 bits wide
  Adder #(.width(32)) adder_1 (
    .a(multiplexer_1_out), .b(multiplexer_2_out), .out({neg, soma_out[30:0]}), .cin(bitselector_1_out));  // open: cout

  assign soma_out[31] = neg;

  // Notes on the sheet:
  //   MUX 1
  //   Detector de número negativo e zero
  //   MUX 2
endmodule

module Shift_Left_24 (
  input  [31:0] data,
  output [31:0] angle___24
);

  Shifter #(.width(32)) shifter_1 (.in(data), .\dist (5'b11000), .out(angle___24));
endmodule

// >>i
module Shift_Right_i (
  input  [31:0] x,
  input  [31:0] y,
  input  rs_shiftr,
  input  [31:0] reg_i,
  output [31:0] shiftr_out,
  output [31:0] nshiftr_out
);

  wire [4:0] bitselector_1_out;
  wire [31:0] multiplexer_1_out;

  Multiplexer #(.width(32), .enable("false")) multiplexer_1 (
    .in0(x), .in1(y), .out(multiplexer_1_out), .sel(rs_shiftr));
  BitSelector #(.width(32), .group(5)) bitselector_1 (.in(reg_i), .out(bitselector_1_out), .sel(3'b000));
  Shifter #(.width(32), .shift("ar")) shifter_1 (.in(multiplexer_1_out), .\dist (bitselector_1_out), .out(shiftr_out));
  assign nshiftr_out = ~shiftr_out;  // NOT_Gate not_1, 32 bits wide
endmodule

// CONTROL PATH
module Control_Path (
  input  zero,
  input  neg,
  input  start,
  input  data_av,
  input  in_5,
  input  in_6,
  output [3:0] Current_State,
  output wr_ang_rs_xySa,
  output wr_it_rs_i,
  output wr_xy,
  output wr_i,
  output wr_sA,
  output wr_xNew_rs_shifr,
  output wr_yNew,
  output done,
  output MEM,
  output [2:0] rs_m1,
  output [2:0] rs_m2
);

  wire next_state_1_s0, next_state_1_s1, next_state_1_s2, next_state_1_s3;

  Next_State next_state_1 (
    .Q3(Current_State[3]), .Q2(Current_State[2]), .Q1(Current_State[1]), .S3(next_state_1_s3),
    .Q0(Current_State[0]), .zero(zero), .neg(neg), .start(start), .S2(next_state_1_s2), .data_av(data_av),
    .S1(next_state_1_s1), .S0(next_state_1_s0));
  D_Flip_Flop S3 (.clk(in_5), .D(next_state_1_s3), .Q(Current_State[3]), .reset(in_6));  // open: Qn, preset, en
  D_Flip_Flop S2 (.clk(in_5), .D(next_state_1_s2), .Q(Current_State[2]), .reset(in_6));  // open: Qn, preset, en
  D_Flip_Flop S1 (.clk(in_5), .D(next_state_1_s1), .Q(Current_State[1]), .reset(in_6));  // open: Qn, preset, en
  D_Flip_Flop S0 (.clk(in_5), .D(next_state_1_s0), .Q(Current_State[0]), .reset(in_6));  // open: Qn, preset, en
  Outputs outputs_1 (
    .wr_ang_rs_xySa(wr_ang_rs_xySa), .wr_it_rs_i(wr_it_rs_i), .wr_xy(wr_xy), .wr_i(wr_i), .wr_sA(wr_sA),
    .wr_xNew_rs_shiftr(wr_xNew_rs_shifr), .wr_yNew(wr_yNew), .done(done), .m1_2(rs_m1[2]), .m1_1(rs_m1[1]),
    .m1_0(rs_m1[0]), .m2_2(rs_m2[2]), .m2_1(rs_m2[1]), .m2_0(rs_m2[0]), .Q3(Current_State[3]),
    .Q2(Current_State[2]), .Q1(Current_State[1]), .Q0(Current_State[0]), .mem(MEM));

  // Other names for the same wires on the sheet: clk = in_5; reset = in_6
endmodule

// DATA PATH
module Data_Path (
  input  [7:0] data,
  input  [31:0] reg_mem,
  input  [2:0] rs_m1,
  input  [2:0] rs_m2,
  input  wr_yNew,
  input  wr_xy,
  input  wr_i,
  input  wr_sA,
  input  clk,
  input  reset,
  input  done,
  input  wr_xNew_rs_shifr,
  input  wr_ang_rs_xySa,
  input  wr_it_rs_i,
  output zero,
  output neg,
  output [31:0] sen,
  output [31:0] i,
  output [31:0] cos
);

  wire [31:0] _24_angle___24, bit_extender_1_out, multiplexer_1_out, multiplexer_2_out, multiplexer_3_out,
       multiplexer_4_out, reg_ang_q, reg_it_q, reg_sumAngle_q, reg_x_q, reg_xNew_q, reg_y_q, reg_yNew_q,
       somador_1_soma_out;

  assign bit_extender_1_out = {{24{1'b0}}, data};  // Bit_Extender bit_extender_1
  Register #(.width(32)) reg_xNew (
    .D(somador_1_soma_out), .en(wr_xNew_rs_shifr), .Q(reg_xNew_q), .clk(clk), .clr(reset));
  Register #(.width(32)) reg_yNew (.D(somador_1_soma_out), .en(wr_yNew), .Q(reg_yNew_q), .clk(clk), .clr(reset));
  Shift_Left_24 _24 (.data(bit_extender_1_out), .angle___24(_24_angle___24));
  Multiplexer #(.width(32), .enable("false")) multiplexer_1 (
    .in0(reg_xNew_q), .in1(32'h9b74ed), .out(multiplexer_1_out), .sel(wr_ang_rs_xySa));
  Multiplexer #(.width(32), .enable("false")) multiplexer_2 (
    .in0(reg_yNew_q), .in1({32{1'b0}}), .out(multiplexer_2_out), .sel(wr_ang_rs_xySa));
  Multiplexer #(.width(32), .enable("false")) multiplexer_3 (
    .in0(somador_1_soma_out), .in1({32{1'b0}}), .out(multiplexer_3_out), .sel(wr_it_rs_i));
  Multiplexer #(.width(32), .enable("false")) multiplexer_4 (
    .in0(somador_1_soma_out), .in1({32{1'b0}}), .out(multiplexer_4_out), .sel(wr_ang_rs_xySa));
  Register #(.width(32)) reg_ang (.D(_24_angle___24), .en(wr_ang_rs_xySa), .Q(reg_ang_q), .clk(clk), .clr(reset));
  Register #(.width(32)) reg_it (.D(bit_extender_1_out), .en(wr_it_rs_i), .Q(reg_it_q), .clk(clk), .clr(reset));
  Register #(.width(32)) reg_x (.D(multiplexer_1_out), .en(wr_xy), .Q(reg_x_q), .clk(clk), .clr(reset));
  Register #(.width(32)) reg_y (.D(multiplexer_2_out), .en(wr_xy), .Q(reg_y_q), .clk(clk), .clr(reset));
  Register #(.width(32)) reg_i (.D(multiplexer_3_out), .en(wr_i), .Q(i), .clk(clk), .clr(reset));
  Register #(.width(32)) reg_sumAngle (.D(multiplexer_4_out), .en(wr_sA), .Q(reg_sumAngle_q), .clk(clk), .clr(reset));
  Somador somador_1 (
    .x(reg_x_q), .y(reg_y_q), .rs_m2(rs_m2), .reg_it(reg_it_q), .rs_m1(rs_m1), .reg_i(i),
    .rs_shiftr(wr_xNew_rs_shifr), .reg_mem(reg_mem), .angle(reg_ang_q), .sumAngle(reg_sumAngle_q), .neg(neg),
    .zero(zero), .soma_out(somador_1_soma_out));
  Register #(.width(32)) reg_sen (.D(reg_y_q), .en(done), .Q(sen), .clk(clk), .clr(reset));
  Register #(.width(32)) reg_cos (.D(reg_x_q), .en(done), .Q(cos), .clk(clk), .clr(reset));
endmodule

// NEXT STATE
module Next_State (
  input  Q3,
  input  Q2,
  input  Q1,
  input  Q0,
  input  zero,
  input  neg,
  input  start,
  input  data_av,
  output S3,
  output S2,
  output S1,
  output S0
);

  wire and_1_out, and_2_out, and_3_out, and_4_out, and_5_out, and_6_out, and_7_out, and_8_out, and_9_out,
       and_10_out, and_11_out, and_12_out, and_13_out, and_14_out, and_15_out, and_16_out, and_17_out,
       not_1_out, not_2_out, not_3_out, not_4_out, not_5_out, not_6_out, not_7_out, not_8_out, not_9_out,
       not_10_out, not_11_out, not_12_out, not_13_out, not_14_out, not_15_out, not_16_out, not_17_out,
       not_18_out, not_19_out, not_20_out, not_21_out, not_22_out, not_23_out, not_24_out, not_25_out,
       not_26_out, not_27_out, not_28_out, not_29_out, not_30_out, not_31_out, not_32_out, not_33_out;

  not not_1 (not_1_out, Q3);
  not not_2 (not_2_out, Q0);
  not not_3 (not_3_out, Q3);
  not not_4 (not_4_out, Q0);
  not not_5 (not_5_out, Q1);
  not not_6 (not_6_out, Q3);
  not not_7 (not_7_out, Q2);
  not not_8 (not_8_out, Q1);
  not not_9 (not_9_out, Q1);
  not not_10 (not_10_out, Q3);
  not not_11 (not_11_out, Q2);
  not not_12 (not_12_out, neg);
  not not_13 (not_13_out, Q0);
  not not_14 (not_14_out, Q1);
  not not_15 (not_15_out, Q1);
  not not_16 (not_16_out, Q3);
  not not_17 (not_17_out, Q2);
  not not_18 (not_18_out, Q1);
  not not_19 (not_19_out, start);
  not not_20 (not_20_out, Q3);
  not not_21 (not_21_out, Q2);
  not not_22 (not_22_out, Q1);
  not not_23 (not_23_out, data_av);
  not not_24 (not_24_out, Q3);
  not not_25 (not_25_out, Q2);
  not not_26 (not_26_out, Q0);
  not not_27 (not_27_out, Q3);
  not not_28 (not_28_out, Q2);
  not not_29 (not_29_out, neg);
  not not_30 (not_30_out, Q1);
  not not_31 (not_31_out, Q0);
  not not_32 (not_32_out, Q1);
  not not_33 (not_33_out, Q0);
  and and_1 (and_1_out, not_1_out, Q1, not_2_out, neg);
  and and_2 (and_2_out, not_3_out, Q1, not_4_out, zero);
  and and_3 (and_3_out, Q2, Q1);
  and and_4 (and_4_out, Q3, not_5_out);
  and and_5 (and_5_out, not_6_out, not_7_out, Q1, Q0);
  or or_1 (S2, and_5_out, and_6_out);
  and and_6 (and_6_out, Q2, not_8_out);
  and and_7 (and_7_out, not_9_out, Q0, start, data_av);
  and and_8 (and_8_out, not_10_out, not_11_out, Q1, not_12_out);
  and and_9 (and_9_out, Q1, not_13_out);
  and and_10 (and_10_out, Q2, not_14_out, Q0);
  and and_11 (and_11_out, Q3, not_15_out, Q0);
  and and_12 (and_12_out, not_16_out, not_17_out, not_18_out, not_19_out, data_av);
  and and_13 (and_13_out, not_20_out, not_21_out, not_22_out, Q0, not_23_out);
  and and_14 (and_14_out, not_24_out, not_25_out, Q1, not_26_out);
  and and_15 (and_15_out, not_27_out, not_28_out, Q1, not_29_out);
  and and_16 (and_16_out, Q2, not_30_out, not_31_out);
  and and_17 (and_17_out, Q3, not_32_out, not_33_out);
  or or_2 (S3, and_1_out, and_2_out, and_3_out, and_4_out);
  or or_3 (S1, and_7_out, and_8_out, and_9_out, and_10_out, and_11_out);
  or or_4 (S0, and_12_out, and_13_out, and_14_out, and_15_out, and_16_out, and_17_out);
endmodule

// OUTPUTS
module Outputs (
  input  Q3,
  input  Q2,
  input  Q1,
  input  Q0,
  output wr_ang_rs_xySa,
  output m1_2,
  output wr_it_rs_i,
  output wr_xy,
  output m1_1,
  output wr_i,
  output m1_0,
  output wr_sA,
  output m2_2,
  output wr_xNew_rs_shiftr,
  output m2_1,
  output wr_yNew,
  output m2_0,
  output mem,
  output done
);

  wire and_1_out, and_2_out, and_3_out, and_4_out, and_8_out, and_9_out, and_10_out, and_11_out, and_12_out,
       and_13_out, and_14_out, and_15_out, and_16_out, and_17_out, and_18_out, and_19_out, and_20_out,
       and_21_out, and_22_out, and_23_out, and_24_out, and_25_out, and_26_out, and_28_out, and_29_out,
       and_30_out, not_1_out, not_2_out, not_3_out, not_4_out, not_5_out, not_6_out, not_7_out, not_8_out,
       not_9_out, not_10_out, not_11_out, not_12_out, not_13_out, not_14_out, not_15_out, not_16_out,
       not_17_out, not_18_out, not_19_out, not_20_out, not_21_out, not_22_out, not_23_out, not_24_out,
       not_25_out, not_26_out, not_27_out, not_28_out, not_29_out, not_30_out, not_31_out, not_32_out,
       not_33_out, not_34_out, not_35_out, not_36_out, not_37_out, not_38_out, not_39_out, not_40_out,
       not_41_out, not_42_out, not_43_out, not_44_out, not_45_out, not_46_out, not_47_out, not_48_out,
       not_49_out, not_50_out;

  not not_1 (not_1_out, Q3);
  not not_2 (not_2_out, Q2);
  not not_3 (not_3_out, Q1);
  not not_4 (not_4_out, Q0);
  not not_5 (not_5_out, Q3);
  not not_6 (not_6_out, Q2);
  not not_7 (not_7_out, Q1);
  not not_8 (not_8_out, Q3);
  not not_9 (not_9_out, Q2);
  not not_10 (not_10_out, Q1);
  not not_11 (not_11_out, Q0);
  not not_12 (not_12_out, Q0);
  not not_13 (not_13_out, Q3);
  not not_14 (not_14_out, Q2);
  not not_15 (not_15_out, Q1);
  not not_16 (not_16_out, Q0);
  not not_17 (not_17_out, Q3);
  not not_18 (not_18_out, Q2);
  not not_19 (not_19_out, Q1);
  not not_20 (not_20_out, Q0);
  not not_21 (not_21_out, Q0);
  not not_22 (not_22_out, Q1);
  and and_1 (and_1_out, Q2, not_23_out, not_24_out);
  not not_23 (not_23_out, Q1);
  not not_24 (not_24_out, Q0);
  and and_2 (and_2_out, Q2, Q1, Q0);
  and and_3 (and_3_out, Q2, not_25_out, Q0);
  not not_25 (not_25_out, Q1);
  and and_4 (and_4_out, Q3, not_26_out, not_27_out);
  not not_26 (not_26_out, Q1);
  not not_27 (not_27_out, Q0);
  and and_5 (done, Q3, Q1, Q0);
  and and_6 (wr_ang_rs_xySa, not_1_out, not_2_out, not_3_out, not_4_out);
  and and_7 (wr_it_rs_i, not_5_out, not_6_out, not_7_out, Q0);
  and and_8 (and_8_out, not_8_out, not_9_out, not_10_out, not_11_out);
  or or_1 (wr_xy, and_8_out, and_9_out);
  and and_9 (and_9_out, Q3, Q1, not_12_out);
  and and_10 (and_10_out, not_13_out, not_14_out, not_15_out, Q0);
  or or_2 (wr_i, and_10_out, and_11_out);
  and and_11 (and_11_out, Q3, Q1, not_16_out);
  and and_12 (and_12_out, not_17_out, not_18_out, not_19_out, not_20_out);
  or or_3 (wr_sA, and_12_out, and_13_out, and_14_out);
  and and_13 (and_13_out, Q2, Q1, not_21_out);
  and and_14 (and_14_out, Q3, not_22_out, Q0);
  or or_4 (wr_xNew_rs_shiftr, and_1_out, and_2_out);
  or or_5 (mem, and_3_out, and_4_out);
  not not_28 (not_28_out, Q2);
  not not_29 (not_29_out, Q0);
  not not_30 (not_30_out, Q3);
  not not_31 (not_31_out, Q2);
  not not_32 (not_32_out, Q0);
  not not_33 (not_33_out, Q1);
  not not_34 (not_34_out, Q1);
  not not_35 (not_35_out, Q0);
  not not_36 (not_36_out, Q3);
  not not_37 (not_37_out, Q2);
  not not_38 (not_38_out, Q0);
  not not_39 (not_39_out, Q1);
  not not_40 (not_40_out, Q0);
  not not_41 (not_41_out, Q3);
  not not_42 (not_42_out, Q2);
  not not_43 (not_43_out, Q1);
  not not_44 (not_44_out, Q0);
  not not_45 (not_45_out, Q1);
  not not_46 (not_46_out, Q2);
  not not_47 (not_47_out, Q3);
  not not_48 (not_48_out, Q1);
  not not_49 (not_49_out, Q1);
  not not_50 (not_50_out, Q0);
  and and_15 (and_15_out, not_28_out, Q1, Q0);
  and and_16 (and_16_out, Q2, Q1, not_29_out);
  and and_17 (and_17_out, Q3, Q0);
  and and_18 (and_18_out, not_30_out, not_31_out, Q1, not_32_out);
  and and_19 (and_19_out, Q2, not_33_out, Q0);
  and and_20 (and_20_out, Q3, not_34_out, not_35_out);
  and and_21 (and_21_out, not_36_out, not_37_out, Q1, not_38_out);
  and and_22 (and_22_out, Q2, not_39_out, not_40_out);
  and and_23 (and_23_out, Q2, Q1, Q0);
  and and_24 (and_24_out, not_41_out, not_42_out, Q1);
  and and_25 (and_25_out, Q2, not_43_out, not_44_out);
  and and_26 (and_26_out, Q3, not_45_out);
  and and_27 (m2_1, not_46_out, Q1);
  and and_28 (and_28_out, not_47_out, Q1, Q0);
  and and_29 (and_29_out, Q2, not_48_out);
  and and_30 (and_30_out, Q3, not_49_out, not_50_out);
  or or_6 (m1_2, and_15_out, and_16_out, and_17_out);
  or or_7 (m1_1, and_18_out, and_19_out, and_20_out);
  or or_8 (m1_0, and_21_out, and_22_out, and_23_out);
  or or_9 (m2_2, and_24_out, and_25_out, and_26_out);
  or or_10 (m2_0, and_28_out, and_29_out, and_30_out);

  assign wr_yNew = mem;
endmodule
